# Fritzing sketch INT_EXP_v0.2 (saved by Fritzing 0.9.2b)
circuit board: 1.54444cm x 3.62229cm
breadboards: 1

parts:
  R2 = Resistor [tolerance=±5% resistance=68 package=THT]
  R2_2 = Resistor [tolerance=±5% resistance=68 package=THT]
  R1 = Resistor [tolerance=±5% resistance=1.5k package=THT]
  C1 = Electrolytic Capacitor [capacitance=0.1µF package="100 mil [THT, electrolytic]"]
  attiny85 = attiny85 [package=dip]
  J2 = screw terminal, 6 pins
  J3 = Screw terminal - 2 pins [package=THT]
  D1 = Zener Diode [part_number=1N4148 breakdown_voltage=3.6V package="300 mil [THT]"]
  D1_2 = Zener Diode [part_number=1N4148 breakdown_voltage=3.6V package="300 mil [THT]"]
  USB = USB Connectors [package=usb-a-h]

nets:
  N1: R2.Pin_0, R1.Pin_0, USB.D-
  N2: R2.Pin_1, attiny85.Pin_5
  N3: R2_2.Pin_0, USB.D+
  N4: R2_2.Pin_1, attiny85.Pin_7
  N5: R1.Pin_1, C1.+, attiny85.Pin_8, D1_2.cathode
  N6: C1.-, attiny85.Pin_4, J2.pin1, J2.pin3, J2.pin5, J3.pin2, USB.GND
  N7: attiny85.Pin_1, J2.pin6
  N8: attiny85.Pin_2, J2.pin4
  N9: attiny85.Pin_3, J2.pin2
  N10: attiny85.Pin_6, J3.pin1
  N11: D1.cathode, D1_2.anode
  N12: D1.anode, USB.VBUS

notes:
  benmoren.com
  +
  -
  INT EXP v0.2
  D+ GREEN
  D- WHITE
  GND  BLACK
  VBUS  RED
  1
